# Fritzing sketch PI2 (saved by Fritzing 0.9.3b)
breadboards: 1

parts:
  U1 = NodeMCU V1.0
  IR1 = TSOP312.., 314.. [package=THT]
  D1 = LTE-302 [package=lte-302]
  Bass_Volume = MCP42xxx [package=so014]
  GY-21 = Digital Temperature Sensor Breakout - TMP102
  Front_Volume = MCP42xxx [package=so014]
  Amplifier = STA540 [package=multiwatt15_yb324gheatsink]
  SPKR1 = Loudspeaker
  U6 = 3.5mm Audio Jack [package=audio-jack-3.5mm-smd]
  SPKR2 = Loudspeaker
  SPKR4 = Loudspeaker
  SPKR3 = Loudspeaker

nets:
  F_CLK: U1.D1, Front_Volume.SCK
  B_CLK: U1.D2, Bass_Volume.SCK
  F_B_DATA: U1.D3, Bass_Volume.DI, Front_Volume.DI
  N1: U1.3V3, IR1.Vs, GY-21.V+
  GND: U1.GND, IR1.GND, D1.C, Bass_Volume.CS, Bass_Volume.GND, Bass_Volume.B1, Bass_Volume.B0, Bass_Volume.DO, GY-21.GND, Front_Volume.CS, Front_Volume.B1, Front_Volume.B0, Front_Volume.DO, Amplifier.P-GND, Amplifier.S-GND, SPKR1.pin2, U6.SLEEVE, SPKR2.pin2, SPKR4.pin2, SPKR3.pin2
  N2: U1.D5, GY-21.SDA
  N3: U1.D6, GY-21.SCL
  N4: U1.D7, D1.A
  N5: U1.RX, IR1.Data
  9V: U1.Vin
  RBV: Bass_Volume.W1, Amplifier.IN3
  N6: Bass_Volume.A1, Front_Volume.A1, U6.RIGHT
  N7: Bass_Volume.A0, Front_Volume.A0, U6.LEFT
  LBV: Bass_Volume.W0, Amplifier.IN4
  5V: Bass_Volume.VCC, Front_Volume.VCC
  RFV: Front_Volume.W1, Amplifier.IN1
  LFV: Front_Volume.W0, Amplifier.IN2
  N8: Amplifier.OUT1, SPKR1.pin1
  N9: Amplifier.OUT2, SPKR2.pin1
  48V: Amplifier.VCC1
  12V: Amplifier.VCC2
  N10: Amplifier.OUT4, SPKR4.pin1
  N11: Amplifier.OUT3, SPKR3.pin1

notes:
  ProJeto Integrador II, Módulo de controle, contendo emisor e receptor IR, sensor de temperatura e humidade e controle de volume

custom parts:
  NodeMCU V1.0: ESP8266 based NodeMCU
